# Fritzing sketch Doorbell (saved by Fritzing 1.0.6)

parts:
  Main_ESP32 = ESP32-DOIT-DEVKIT-V1-36pin_1
  Cam_Online_led = LEDs [package=led10mm]
  Microphone_(Built-in_to_sense) = MIC [package=mic_electret_smd]
  Xiao_sense_Camera = prefix8089 [chip_label=ESP32S3(sense)]
  Doorbell_Button = Round Pushbutton
  Call_Button = Round Pushbutton
  Ready_LED = LEDs [package=led10mm]
  WARN_led = LEDs [package=led10mm]
  LCD1 = 1_54in tft lcd
  NFC = PN532 Elechouse RFID NFC Module V3
  Amp_module = ESP32-S3-DevKitC-1-N8R8-v1 [part_number=ESP32-S3-DevKitC-1-N8R8-v1]
  AMP = Stereo 3.7W Class D Amplifier [mn="Maxim Integrated" mpn=MAX98357BETE+ package=16-TQFN]
  SP1 = SPEAKER [package=pcb_mount_speaker]
  R1 = Resistor [tolerance=±5% resistance=220 package="2512 [SMD]"]
  Speaker_LED = LEDs [package=led10mm]

nets:
  N1: Main_ESP32.connector3, Call_Button.leg1
  N2: Main_ESP32.connector4, Doorbell_Button.leg1
  N3: Main_ESP32.connector7, Xiao_sense_Camera.connector7
  N4: Main_ESP32.connector8, Xiao_sense_Camera.connector8
  N5: Main_ESP32.connector9, Xiao_sense_Camera.connector9
  N6: Main_ESP32.connector10, Xiao_sense_Camera.connector2
  N7: Main_ESP32.connector12, NFC.SDA
  N8: Main_ESP32.connector16, Cam_Online_led.C, Xiao_sense_Camera.connector12, Ready_LED.C, WARN_led.C, LCD1.pin_1, NFC.GND, Amp_module.pin_22, Amp_module.pin_24, Amp_module.pin_44, AMP.GND#2, AMP.SD_MODE, R1.Pin_1, Speaker_LED.C
  N9: Main_ESP32.connector17, Xiao_sense_Camera.connector13, LCD1.pin2, LCD1.pin_8, NFC.VCC, Amp_module.pin_21
  N10: Main_ESP32.connector18, Doorbell_Button.leg0, Call_Button.leg0
  N11: Main_ESP32.connector23, NFC.SCL
  N12: Main_ESP32.connector24, Ready_LED.A
  N13: Main_ESP32.connector25, WARN_led.A
  N14: Main_ESP32.connector26, Xiao_sense_Camera.connector5
  N15: Main_ESP32.connector27, Xiao_sense_Camera.connector6
  N16: Main_ESP32.connector28, NFC.IRQ
  N17: Main_ESP32.connector29, LCD1.pin_5
  N18: Main_ESP32.connector30, LCD1.pin_6
  N19: Main_ESP32.connector31, LCD1.pin_7
  N20: Main_ESP32.connector34, LCD1.pin3
  N21: Main_ESP32.connector35, LCD1.pin4
  N22: Cam_Online_led.A, Xiao_sense_Camera.connector1
  N23: Microphone_(Built-in_to_sense).1, Xiao_sense_Camera.connector14
  N24: Microphone_(Built-in_to_sense).2, Xiao_sense_Camera.connector15
  N25: Amp_module.pin_6, Speaker_LED.A
  N26: Amp_module.pin_7, AMP.LRCLK
  N27: Amp_module.pin_12, AMP.BCLK
  N28: Amp_module.pin_15, AMP.DIN
  N29: AMP.GAIN__SLOT, R1.Pin_0
  N30: AMP.OUTP, SP1.+
  N31: AMP.GND#10, SP1.-

custom parts:
  1_54in tft lcd: This is the DONGKER 1.54'' LCD Display Module, SPI 240x240 1.54'' LCD Display Module ST7789 Driver 240x240 3.3V IPS LCD Display Screen Module. The 1.54" display has 240x240 color pixels.
  PN532 Elechouse RFID NFC Module V3: NFC is a popular technology in recent years. We often heard this work while smart phone company such as Samsung or HTC introduces their latest high-end phones. Almost all the high-end phone in the market support NFC. Near field communication (NFC) is a set of standards for smart phones and similar devices to establish radio communication with each other by touching them together or bringing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
  ESP32-S3-DevKitC-1-N8R8-v1: ESP32-S3-DevKitC-1-N8R8-v1 This module is 44pins long (2x22) and 11 pins width.
  Stereo 3.7W Class D Amplifier: Mono 3.2W Class D Amplifier Datasheet: https://datasheets.maximintegrated.com/en/ds/MAX98357A-MAX98357B.pdf The MAX98357B is an easy-to-use, low-cost, digital pulse-code modulation (PCM) input Class D amplifier that provides industry-leading Class AB audio performance with Class D efficiency. The digital audio interface automatically recognizes up to 35 different PCM and TDM clocking schemes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
